# Fritzing sketch Skematik (saved by Fritzing 0.9.3b)

parts:
  M1 = DOIT Esp32 DevKit v1 (30 pins long, 11 pins width) [part_number=ESP32S-PIN30]
  M2 = 1 chan 5v relay module
  TP1 = TP4056 [chip_label=TP4056 package="DIP (Dual Inline) [THT]"]
  Part1 = SRF05 Ultrasonic Rangefinder
  SW1 = Slide_Switch_new
  OLED1 = OLED 128x64 I2C Monochrome Display
  M3 = fc-51 [package=THT]
  M4 = Getriebemotor
  M5 = fc-51 [package=THT]
  M6 = Getriebemotor
  U2 = BATTERY-2 [package=battery-aaa]
  U4 = BATTERY-2 [package=battery-aaa]
  U5 = BATTERY-2 [package=battery-aaa]
  SW2 = Slide_Switch_new
  U6 = BATTERY-2 [package=battery-aaa]
  M7 = MT3608 Module
  M8 = MT3608 Module
  L298N1 = L298N DC motor driver
  M9 = NEO-6M GPS Module [part_number=GY-GPS6MV2]
  S1 = Pushbutton [package=THT]
  S2 = Pushbutton [package=THT]
  S3 = Pushbutton [package=THT]
  S4 = Pushbutton [package=THT]
  M10 = Getriebemotor
  M11 = Getriebemotor
  M12 = DOIT Esp32 DevKit v1 (30 pins long, 11 pins width) [part_number=ESP32S-PIN30]
  LED1 = smd LED [color="Red (633nm)" package="1206 [SMD]"]
  LED2 = smd LED [color="Red (633nm)" package="1206 [SMD]"]
  LED3 = smd LED [color="Red (633nm)" package="1206 [SMD]"]
  LED4 = smd LED [color="Red (633nm)" package="1206 [SMD]"]
  R1 = Resistor [tolerance=±5% resistance=220 package=THT]
  R2 = Resistor [tolerance=±5% resistance=220 package=THT]
  R3 = Resistor [tolerance=±5% resistance=220 package=THT]
  R4 = Resistor [tolerance=±5% resistance=220 package=THT]

nets:
  GND: M1.GND, Part1.GND, M3.pin2, M5.pin2, U5.-1, M8.pin4, L298N1.GND, LED1.cathode, LED2.cathode, LED3.cathode
  N1: M1.D4, L298N1.ENB
  N2: M1.D18, L298N1.IN4
  N3: M1.D19, L298N1.IN3
  N4: M1.D21, L298N1.IN2
  N5: M1.D22, L298N1.IN1
  N6: M1.D23, L298N1.ENA
  N7: M1.D26, M3.pin1
  N8: M1.D27, Part1.Trig
  N9: M1.D14, Part1.Echo
  N10: M1.D13, M5.pin1
  VIN: M1.VIN, Part1.VCC, M3.pin3, M5.pin3, M8.pin3
  VDD: M2.pin_1, OLED1.VDD, M9.Vcc, M12.3V3
  GND_2: M2.pin_2, OLED1.GND, M7.pin4, M9.GND, M12.GND
  N11: M2.pin_3, M12.D13
  N12: M2.pin_5, U4.+1
  N13: M2.pin_6, L298N1.12V, LED1.anode, LED4.anode
  N14: TP1.pin3, U2.+1, SW2.pin_2, U6.+1
  N15: TP1.pin6, U2.-1, U6.-1, M7.pin1, M8.pin1, S1.leg1, S2.leg1, S3.leg1, S4.leg1
  N16: SW1.pin_1, U5.+1
  N17: SW1.pin_2, U4.-1
  N18: OLED1.SCK, M12.D22
  N19: OLED1.SDA, M12.D21
  N20: M4.pin_1, L298N1.OUT1, M10.pin_2
  N21: M4.pin_2, L298N1.OUT2, M10.pin_1
  N22: M6.pin_1, L298N1.OUT4, M11.pin_2
  N23: M6.pin_2, L298N1.OUT3, M11.pin_1
  N24: SW2.pin_1, M7.pin2, M8.pin2
  N25: M7.pin3, M12.VIN, R1.Pin_1
  N26: M9.Tx, M12.D4
  N27: M9.Rx, M12.D2
  N28: M12.D32, R4.Pin_0
  N29: M12.D33, R3.Pin_0
  N30: M12.D25, R2.Pin_0
  N31: M12.D26, R1.Pin_0

notes:
  5V
  8V

custom parts:
  DOIT Esp32 DevKit v1 (30 pins long, 11 pins width): The DOIT Esp32 DevKit v1 is one of the development board created by DOIT to evaluate the ESP-WROOM-32 module. It is based on the ESP32 microcontroller that boasts Wifi, Bluetooth, Ethernet and Low Power support all in a single chip. (vanepp) made breadboard work, adjusted pin numbering and labels and reduced size of schematic and cleaned up pcb. This chip is 30pins long (2 x15) and 11 pins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
  1 chan 5v relay module: 1 Channel 5V Relay Module Board Shield with Optocoupler Support High and Low Level Trigger for Arduino.
  TP4056: A DIP stand-in part for whatever IC you want. With 6 pins on a 300mil dual inline package (DIP) footprint.
  Slide_Switch_new: the New two pin slide switch
  MT3608 Module: MT3608 Boost Converter Module Links: Aerosemi MT3608 2A Step Up Converter datasheet
  L298N DC motor driver: 2x DC motor driver with 78M05 positive voltage regulator (7..35 V) L298N: max 46 V, 2 A Set 5 V Enable jumper to enable 5 V regultor (needed for the L298N) and +5 V output at screw terminal or supply external +5 V at screw terminal Set ENA and/or ENB to +5 V to enable motor permanently or supply ENA and/or ENB with PWM signal IN1 and IN2 set rotation directory for motor A (OUT1/OUT2) IN2 and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
  NEO-6M GPS Module: GY-GPS6MV2 NEO-6M GPS Module Module based on U-blox NEO-6M GPS engine, incorporating regulator for 3.3-5V DC input, MS621FE-compatible rechargeable battery for backup and EEPROM for storing configuration settings. Links: NEO-6 series product information page NEO-6 Datasheet
